# Fritzing sketch labelsFritzing (saved by Fritzing 0.9.3b)
breadboards: 1

parts:
  Part1 = Arduino Uno (Rev3)
  Part2 = Thermal Printer
  Part3 = LilyPad Button Board

nets:
  N1: Part1.A1, Part1.3V3, Part3.S
  N2: Part1.GND, Part2.GND#2, Part3.-
  N3: Part1.D2, Part2.RXD
  N4: Part1.D3_PWM, Part2.TXD

notes:
  5V-9V Power supply
  1.5A
